# Fritzing sketch Neopixel Raspberry Pi HAT v7 (saved by Fritzing 0.9.3b)
circuit board: 6.50001cm x 5.64998cm
breadboards: 1

parts:
  J2 = shrouded pin header, 40 pins [form="♂ (shrouded male)"]
  R5 = Resistor [tolerance=±5% resistance=220 package=THT]
  R4 = Resistor [tolerance=±5% resistance=220 package=THT]
  R3 = Resistor [tolerance=±5% resistance=220 package=THT]
  LED3 = LED - 5mm [color="Red (633nm)" package="5 mm [THT]"]
  LED4 = LED - 5mm [color="Red (633nm)" package="5 mm [THT]"]
  LED5 = LED - 5mm [color="Red (633nm)" package="5 mm [THT]"]
  R2 = Resistor [tolerance=±5% resistance=220 package=THT]
  LED2 = LED - 5mm [color="Red (633nm)" package="5 mm [THT]"]
  R1 = Resistor [tolerance=±5% resistance=220 package=THT]
  LED1 = LED - 5mm [color="Red (633nm)" package="5 mm [THT]"]
  ATMEGA328 = atmega328 [package=dip]
  LED_OUTPUT = screw terminal, 3 pins
  5v/D0/GND1 = double row female pin header, 8 pins [form="♀ (female)"]
  R6 = Resistor [tolerance=±5% resistance=220 package=THT]
  S1 = Toggle Switch [package=THT]

nets:
  N1: J2.pin2, ATMEGA328.A4, 5v/D0/GND1.pin3, 5v/D0/GND1.pin6
  N2: J2.pin3, ATMEGA328.A5, 5v/D0/GND1.pin2, 5v/D0/GND1.pin7
  N3: J2.pin20, LED3.cathode, LED4.cathode, LED5.cathode, LED2.cathode, LED1.cathode, ATMEGA328.GND, LED_OUTPUT.pin3, 5v/D0/GND1.pin4, 5v/D0/GND1.pin5
  N4: J2.pin40, ATMEGA328.VCC, ATMEGA328.AVCC, 5v/D0/GND1.pin1, 5v/D0/GND1.pin8, S1.L1
  N5: R5.Pin_0, ATMEGA328.D9_(PWM)
  N6: R5.Pin_1, LED5.anode
  N7: R4.Pin_0, ATMEGA328.D10_(PWM)
  N8: R4.Pin_1, LED4.anode
  N9: R3.Pin_0, ATMEGA328.D11_(PWM)
  N10: R3.Pin_1, LED3.anode
  N11: R2.Pin_0, ATMEGA328.D12
  N12: R2.Pin_1, LED2.anode
  N13: R1.Pin_0, ATMEGA328.D13
  N14: R1.Pin_1, LED1.anode
  N15: ATMEGA328.D4, R6.Pin_1
  N16: LED_OUTPUT.pin1, S1.COM
  N17: LED_OUTPUT.pin2, R6.Pin_0

notes:
  Neopixel Raspberry PI HAT version 7
