# Fritzing sketch pcb v2 (saved by Fritzing 0.9.3b)
circuit board: 6.50001cm x 5.64998cm
breadboards: 1

parts:
  J2 = shrouded pin header, 40 pins [form="♂ (shrouded male)"]
  U1 = atmega328 [package=dip]
  LED1 = LED - 3mm [color="Red (633nm)" package="3 mm [THT]"]
  R1 = Resistor [tolerance=±5% resistance=220 package=THT]
  R2 = Resistor [tolerance=±5% resistance=220 package=THT]
  J14 = female pin header, 2 pins [form="♀ (female)"]
  74HCT08 = 74HC08 Logic AND Gate [part_number=74HCT08 package="DIP (Dual Inline) [THT]"]
  C1 = Electrolytic Capacitor [capacitance=10µF package="100 mil [THT, electrolytic]"]
  J13 = female pin header, 3 pins [form="♀ (female)"]

nets:
  N1: J2.pin2, U1.A4
  N2: J2.pin3, U1.A5
  N3: J2.pin9, U1.VCC, U1.AVCC
  GND: J2.pin20, U1.GND, LED1.cathode, J14.pin2, 74HCT08.GND, C1.-, J13.pin3
  N4: J2.pin40, 74HCT08.VCC
  N5: U1.D4, 74HCT08.1A, 74HCT08.1B
  N6: U1.D9_(PWM), R1.Pin_0
  N7: LED1.anode, R1.Pin_1
  N8: R2.Pin_0, J13.pin2
  N9: R2.Pin_1, 74HCT08.1Y
  N10: J14.pin1, C1.+, J13.pin1

notes:
  Output
  Input
