# Fritzing sketch pcb (saved by Fritzing 0.9.3b)
circuit board: 6.50001cm x 5.64998cm
breadboards: 1

parts:
  J2 = shrouded pin header, 40 pins [form="♂ (shrouded male)"]
  ATTINY85 = attiny85 [package=dip]
  R5 = Resistor [tolerance=±5% resistance=220 package=THT]
  LED1 = LED - 3mm [color="Red (633nm)" package="3 mm [THT]"]
  R1 = Resistor [tolerance=±5% resistance=220 package=THT]
  ATTINY85_2 = attiny85 [package=dip]
  R2 = Resistor [tolerance=±5% resistance=220 package=THT]
  R3 = Resistor [tolerance=±5% resistance=220 package=THT]
  R4 = Resistor [tolerance=±5% resistance=220 package=THT]
  SW1 = DIP SWITCH [package=dipswitch-02]
  SW2 = DIP SWITCH [package=dipswitch-02]
  J13 = female pin header, 3 pins [form="♀ (female)"]
  J14 = female pin header, 2 pins [form="♀ (female)"]
  74HCT08 = 74HC08 Logic AND Gate [part_number=74HCT08 package="DIP (Dual Inline) [THT]"]

nets:
  N1: J2.pin2, ATTINY85.Pin_5
  N2: J2.pin3, ATTINY85.Pin_7
  N3: J2.pin5, ATTINY85.Pin_1, ATTINY85.Pin_4, LED1.cathode, R1.Pin_0, ATTINY85_2.Pin_1, ATTINY85_2.Pin_4, R2.Pin_0, R3.Pin_0, R4.Pin_0, J13.pin3, J14.pin2, 74HCT08.GND
  N4: J2.pin9, ATTINY85.Pin_8, ATTINY85_2.Pin_8, SW1.1, SW1.2, SW2.1, SW2.2
  N5: J2.pin40, J13.pin1, J14.pin1, 74HCT08.VCC
  N6: ATTINY85.Pin_2, 74HCT08.1A, 74HCT08.1B
  N7: ATTINY85.Pin_3, ATTINY85_2.Pin_6
  N8: ATTINY85.Pin_6, R5.Pin_1
  N9: R5.Pin_0, LED1.anode
  N10: R1.Pin_1, ATTINY85_2.Pin_2, SW1.3
  N11: ATTINY85_2.Pin_3, R2.Pin_1, SW1.4
  N12: ATTINY85_2.Pin_5, R4.Pin_1, SW2.4
  N13: ATTINY85_2.Pin_7, R3.Pin_1, SW2.3
  N14: J13.pin2, 74HCT08.1Y

notes:
  Output
  Input
  Neopixel Raspberry PI HAT version 5
